// Logisim project booth multiplier.circ as structural Verilog: 3 circuits, main circuit 11b booth multiply stage
module _11b_booth_multiply_stage (
  input  [10:0] p,
  input  lsb,
  input  y1,
  input  y2,
  input  [10:0] x,
  output msb,
  output [10:0] p_2,
  output [10:0] x_2
);

  wire or_1_out;
  wire [0:0] and_1_out;
  wire [1:0] multiplexer_1_out, not_1_out;
  wire [10:0] multiplexer_2_out, multiplexer_3_out, not_2_out, shifter_2_out;

  Multiplexer #(.width(2), .enable("false")) multiplexer_1 (
    .in0({y1, lsb}), .in1(not_1_out), .out(multiplexer_1_out), .sel(y2));
  assign not_1_out = ~{y1, lsb};  // NOT_Gate not_1, 2 bits wide
  or or_1 (or_1_out, multiplexer_1_out[1], multiplexer_1_out[0]);
  Multiplexer #(.width(11), .enable("false")) multiplexer_2 (
    .in0({11{1'b0}}), .in1(x), .out(multiplexer_2_out), .sel(or_1_out));
  Shifter #(.width(11)) shifter_1 (.in(x), .\dist (4'b0010), .out(x_2));
  and and_1 (and_1_out[0], multiplexer_1_out[1], multiplexer_1_out[0]);
  Shifter #(.width(11)) shifter_2 (.in(multiplexer_2_out), .\dist ({3'b000, and_1_out[0]}), .out(shifter_2_out));
  assign not_2_out = ~shifter_2_out;  // NOT_Gate not_2, 11 bits wide
  Adder #(.width(11)) adder_1 (.a(p), .b(multiplexer_3_out), .out(p_2), .cin(y2));  // open: cout
  Multiplexer #(.width(11), .enable("false")) multiplexer_3 (
    .in0(shifter_2_out), .in1(not_2_out), .out(multiplexer_3_out), .sel(y2));

  assign msb = y2;

  // Notes on the sheet:
  //   for vhdl
  //   generic n-input inverter
  //   generic n-size adder
  //   generic n-input 1 bit left-shifter
  //   generic n-input 2 bit left-shifter
  //   2-1mux that can handle n-sized input/output
  //   Note: does effectively use an adder subtractor, because mux with inverter is effectively an xor
endmodule

module _11b_booth_multiply_w__xor (
  input  [10:0] p,
  input  lsb,
  input  y1,
  input  y2,
  input  [10:0] x,
  output msb,
  output [10:0] p_2,
  output [10:0] x_2
);

  wire or_1_out;
  wire [0:0] and_1_out;
  wire [1:0] xor_1_out;
  wire [10:0] multiplexer_1_out, shifter_2_out, xor_2_out;

  or or_1 (or_1_out, xor_1_out[1], xor_1_out[0]);
  assign xor_1_out = {y1, lsb} ^ {2{y2}};  // XOR_Gate xor_1, 2 bits wide
  and and_1 (and_1_out[0], xor_1_out[1], xor_1_out[0]);
  Multiplexer #(.width(11), .enable("false")) multiplexer_1 (
    .in0({11{1'b0}}), .in1(x), .out(multiplexer_1_out), .sel(or_1_out));
  Shifter #(.width(11)) shifter_1 (.in(x), .\dist (4'b0010), .out(x_2));
  Shifter #(.width(11)) shifter_2 (.in(multiplexer_1_out), .\dist ({3'b000, and_1_out[0]}), .out(shifter_2_out));
  assign xor_2_out = {11{y2}} ^ shifter_2_out;  // XOR_Gate xor_2, 11 bits wide
  Adder #(.width(11)) adder_1 (.a(p), .b(xor_2_out), .out(p_2), .cin(y2));  // open: cout

  assign msb = y2;

  // Notes on the sheet:
  //   for vhdl
  //   generic n-input inverter
  //   generic n-size adder
  //   generic n-input 1 bit left-shifter
  //   generic n-input 2 bit left-shifter
  //   2-1mux that can handle n-sized input/output
  //   Note: does effectively use an adder subtractor, because mux with inverter is effectively an xor
endmodule

module using_booth_multiply (
  input  [5:0] y,
  input  [5:0] x,
  output [10:0] out_3
);

  wire n11b_booth_multiply_stage_2_msb, n11b_booth_multiply_stage_3_msb;
  wire [10:0] n11b_booth_multiply_stage_2_p_2, n11b_booth_multiply_stage_2_x_2,
       n11b_booth_multiply_stage_3_p_2, n11b_booth_multiply_stage_3_x_2;

  _11b_booth_multiply_stage u_11b_booth_multiply_stage_1 (
    .p(n11b_booth_multiply_stage_2_p_2), .lsb(n11b_booth_multiply_stage_2_msb), .y1(y[4]), .y2(y[5]),
    .p_2(out_3), .x(n11b_booth_multiply_stage_2_x_2));  // open: msb, x_2
  _11b_booth_multiply_stage u_11b_booth_multiply_stage_2 (
    .p(n11b_booth_multiply_stage_3_p_2), .lsb(n11b_booth_multiply_stage_3_msb), .y1(y[2]), .y2(y[3]),
    .msb(n11b_booth_multiply_stage_2_msb), .p_2(n11b_booth_multiply_stage_2_p_2),
    .x(n11b_booth_multiply_stage_3_x_2), .x_2(n11b_booth_multiply_stage_2_x_2));
  _11b_booth_multiply_stage u_11b_booth_multiply_stage_3 (
    .p({11{1'b0}}), .lsb(1'b0), .y1(y[0]), .y2(y[1]), .msb(n11b_booth_multiply_stage_3_msb),
    .p_2(n11b_booth_multiply_stage_3_p_2), .x({{6{x[5]}}, x[4:0]}), .x_2(n11b_booth_multiply_stage_3_x_2));

  // Notes on the sheet:
  //   in class design
  //   X=001010 (10) & Y=101011 (-21)
  //   = 111 0010 1110 (-210)
endmodule
